// Logisim project OptimizedCPU.circ as structural Verilog: 3 circuits, main circuit main
module main (
  input  in_1
);

  wire and_1_out, and_2_out, clock_1_out, cpu_1_rd, cpu_1_we, cpu_1_wr_0, cpu_1_wr_1, d_ff_1_q,
       keyboard_1_avail, not_1_out, not_2_out, or_1_out;
  wire [6:0] bit_extender_2_out, keyboard_1_data;
  wire [7:0] bit_extender_1_out, cpu_1_data_o, cpu_1_oport_d, ram_1_dout, undriven;
  wire [21:0] cpu_1_addr;

  Keyboard keyboard_1 (
    .clk(clock_1_out), .re(and_1_out), .clr(and_2_out), .avail(keyboard_1_avail), .data(keyboard_1_data));
  and and_1 (and_1_out, not_1_out, cpu_1_rd);
  not not_1 (not_1_out, clock_1_out);
  and and_2 (and_2_out, not_2_out, cpu_1_rd);
  not not_2 (not_2_out, cpu_1_rd);
  Random random_1 ();  // open: clk, next, out, clr
  assign bit_extender_1_out = {{1{1'b0}}, keyboard_1_data};  // Bit_Extender bit_extender_1
  D_Flip_Flop d_ff_1 (.Q(d_ff_1_q), .reset(cpu_1_wr_1));  // open: clk, D, Qn, preset
  or or_1 (or_1_out, keyboard_1_avail, d_ff_1_q);
  Clock clock_1 (.out(clock_1_out));
  CPU cpu_1 (
    .rd(cpu_1_rd), .wr_0(cpu_1_wr_0), .wr_1(cpu_1_wr_1), .addr(cpu_1_addr), .we(cpu_1_we),
    .DATA_o(cpu_1_data_o), .oPORT_d(cpu_1_oport_d), .inp_sig(or_1_out), .iPORT_0(bit_extender_1_out),
    .iPORT_1(undriven), .rst(in_1), .DATA_i(ram_1_dout), .clk(clock_1_out));  // open: wr_2, wr_3, iPORT_2, iPORT_3
  Bit_Extender #(.out_width(7)) bit_extender_2 (.in(cpu_1_oport_d), .out(bit_extender_2_out));
  TTY tty_1 (.data(bit_extender_2_out), .clk(clock_1_out), .we(cpu_1_wr_0), .clr(in_1));
  RAM #(.addrWidth(22)) ram_1 (
    .addr(cpu_1_addr), .we(cpu_1_we), .oe(1'b1), .clk(clock_1_out), .din(cpu_1_data_o), .dout(ram_1_dout));
endmodule

module CPU (
  input  [7:0] iPORT_0,
  input  [7:0] iPORT_1,
  input  [7:0] iPORT_2,
  input  inp_sig,
  input  [7:0] iPORT_3,
  input  [7:0] DATA_i,
  input  rst,
  input  clk,
  output rd,
  output wr_0,
  output wr_1,
  output wr_2,
  output wr_3,
  output [7:0] oPORT_d,
  output [21:0] addr,
  output we,
  output [7:0] DATA_o
);

  wire adder_1_cout, and_1_out, and_3_out, and_4_out, and_8_out, and_9_out, and_10_out, and_11_out,
       and_12_out, and_13_out, and_14_out, and_15_out, and_16_out, and_17_out, and_18_out, and_19_out,
       and_20_out, and_21_out, and_22_out, and_27_out, c, decoder_1_out0, decoder_1_out1, decoder_1_out3,
       decoder_2_out1, decoder_2_out2, decoder_2_out3, decoder_3_out0, decoder_3_out1, decoder_3_out2,
       decoder_3_out3, decoder_3_out4, decoder_3_out5, decoder_3_out6, decoder_3_out7, decoder_4_out0,
       decoder_4_out1, decoder_4_out2, decoder_4_out3, decoder_5_out0, decoder_5_out1, decoder_5_out2,
       decoder_5_out3, decoder_5_out4, decoder_5_out5, decoder_5_out6, decoder_5_out7, decoder_6_out0,
       decoder_6_out1, inp, n, nand_1_out, nor_1_out, nor_2_out, not_1_out, not_2_out, not_4_out, not_5_out,
       not_6_out, not_7_out, not_8_out, not_9_out, not_10_out, not_11_out, not_12_out, not_13_out,
       not_14_out, not_15_out, or_1_out, or_2_out, or_3_out, or_4_out, or_5_out, or_6_out, or_7_out,
       or_10_out, or_11_out, or_13_out, wi, z, zi;
  wire [1:0] priority_encoder_1_out, rom_1_data_2, rom_1_data_3;
  wire [2:0] counter_1_q, register_3_q;
  wire [2:2] or_8_out, or_9_out;
  wire [4:0] OP;
  wire [5:0] bit_extender_7_out;
  wire [7:0] adder_1_out, and_2_out, and_5_out, bit_extender_1_out, bit_extender_2_out, bit_extender_3_out,
       bit_extender_4_out, multiplexer_1_out, multiplexer_5_out, not_3_out, register_4_q, register_5_q,
       register_6_q, register_7_q, register_8_q, register_9_q, register_12_q, register_13_q, register_14_q,
       xor_1_out, xor_2_out, xor_3_out;
  wire [15:0] adder_2_out, bit_extender_5_out, bit_extender_6_out, controlled_buffer_8_out,
       multiplexer_2_out, multiplexer_3_out, multiplexer_4_out, register_10_q, register_11_q, wz;
  wire [21:0] rom_1_data;

  not not_1 (not_1_out, inp);
  nand nand_1 (nand_1_out, not_1_out, rd);
  and and_1 (and_1_out, nand_1_out, clk);
  or or_1 (or_1_out, nor_2_out, rst);
  Register register_1 (.D(oPORT_d), .en(wi), .clk(and_1_out), .Q(wz[15:8]));  // open: clr
  Register register_2 (.D(oPORT_d), .en(zi), .clk(and_1_out), .Q(wz[7:0]));  // open: clr
  Counter #(.max('h7), .width(3)) counter_1 (
    .clr(or_1_out), .up(1'b1), .count(1'b1), .clk(not_2_out), .Q(counter_1_q));  // open: load, D, carry
  not not_2 (not_2_out, and_1_out);
  assign xor_1_out = wz[15:8] ^ bit_extender_1_out;  // XOR_Gate xor_1, 8 bits wide
  assign not_3_out = ~bit_extender_2_out;  // NOT_Gate not_3, 8 bits wide
  assign bit_extender_1_out = {{7{rom_1_data[21]}}, rom_1_data[21]};  // Bit_Extender bit_extender_1
  assign bit_extender_2_out = {{7{rom_1_data[20]}}, rom_1_data[20]};  // Bit_Extender bit_extender_2
  assign bit_extender_3_out = {{7{rom_1_data[19]}}, rom_1_data[19]};  // Bit_Extender bit_extender_3
  assign and_2_out = wz[7:0] & not_3_out;  // AND_Gate and_2, 8 bits wide
  assign xor_2_out = and_2_out ^ bit_extender_3_out;  // XOR_Gate xor_2, 8 bits wide
  assign bit_extender_4_out = {{7{rom_1_data[17]}}, rom_1_data[17]};  // Bit_Extender bit_extender_4
  and and_3 (and_3_out, decoder_1_out1, and_1_out);
  and and_4 (and_4_out, rom_1_data[16], c);
  Adder adder_1 (.a(xor_1_out), .b(xor_2_out), .out(adder_1_out), .cin(and_4_out), .cout(adder_1_cout));
  assign and_5_out = xor_1_out & xor_2_out;  // AND_Gate and_5, 8 bits wide
  D_Flip_Flop d_ff_1 (.clk(and_3_out), .D(adder_1_cout), .Q(c));  // open: Qn, preset, reset
  Multiplexer #(.width(8)) multiplexer_1 (
    .in0(adder_1_out), .in1(and_5_out), .out(multiplexer_1_out), .sel(rom_1_data[18]));
  assign xor_3_out = multiplexer_1_out ^ bit_extender_4_out;  // XOR_Gate xor_3, 8 bits wide
  or or_2 (or_2_out, xor_3_out[7], xor_3_out[6]);
  or or_3 (or_3_out, xor_3_out[5], xor_3_out[4]);
  or or_4 (or_4_out, xor_3_out[3], xor_3_out[2]);
  or or_5 (or_5_out, or_2_out, or_3_out);
  nor nor_1 (nor_1_out, or_5_out, or_7_out);
  D_Flip_Flop d_ff_2 (.clk(and_3_out), .D(xor_3_out[7]), .Q(n));  // open: Qn, preset, reset
  D_Flip_Flop d_ff_3 (.clk(and_3_out), .D(nor_1_out), .Q(z));  // open: Qn, preset, reset
  ROM #(.dataWidth(22)) rom_1 (
    .addr({counter_1_q, OP}),
    .data({rom_1_data[21:16], rom_1_data_3, rom_1_data[13:12], rom_1_data_2, rom_1_data[9:0]}));
  assign oPORT_d = decoder_1_out1 ? xor_3_out : 8'bz;  // Controlled_Buffer controlled_buffer_1
  or or_6 (or_6_out, xor_3_out[1], xor_3_out[0]);
  or or_7 (or_7_out, or_4_out, or_6_out);
  Decoder #(.enable("false"), .select(2)) decoder_1 (
    .out0(decoder_1_out0), .out1(decoder_1_out1), .out2(rd), .out3(decoder_1_out3), .sel(rom_1_data_3));
  Decoder #(.enable("false"), .select(2)) decoder_2 (
    .out1(decoder_2_out1), .out2(decoder_2_out2), .out3(decoder_2_out3), .sel(rom_1_data[13:12]));  // open: out0
  not not_4 (not_4_out, rom_1_data[8]);
  and and_6 (wi, rom_1_data[8], decoder_2_out1);
  and and_7 (zi, not_4_out, decoder_2_out1);
  nor nor_2 (nor_2_out, rom_1_data_3[0], rom_1_data_3[1], rom_1_data[12], rom_1_data[13], rom_1_data_2[0], rom_1_data_2[1], rom_1_data[1], rom_1_data[0]);
  not not_5 (not_5_out, clk);
  Register register_3 (.D(oPORT_d), .en(decoder_2_out3), .clk(and_1_out), .Q({OP, register_3_q}), .clr(rst));
  D_Flip_Flop d_ff_4 (.clk(clk), .D(1'b0), .Q(inp), .preset(and_8_out));  // open: Qn, reset
  and and_8 (and_8_out, not_5_out, inp_sig);
  Register register_4 (.D(oPORT_d), .en(rom_1_data[4]), .clk(and_1_out), .Q(register_4_q), .clr(rst));
  and and_9 (and_9_out, OP[4], OP[3]);
  not not_6 (not_6_out, decoder_2_out1);
  and and_10 (and_10_out, not_6_out, rom_1_data[8]);
  and and_11 (and_11_out, OP[2], and_9_out);
  and and_12 (and_12_out, OP[1], and_9_out);
  and and_13 (and_13_out, OP[0], and_9_out);
  not not_7 (not_7_out, and_11_out);
  not not_8 (not_8_out, and_12_out);
  and and_14 (and_14_out, not_7_out, not_8_out, not_9_out);
  not not_9 (not_9_out, and_13_out);
  not not_10 (not_10_out, and_11_out);
  not not_11 (not_11_out, and_12_out);
  and and_15 (and_15_out, not_10_out, not_11_out, and_13_out);
  not not_12 (not_12_out, and_11_out);
  and and_16 (and_16_out, not_12_out, and_12_out, not_13_out);
  not not_13 (not_13_out, and_13_out);
  Decoder #(.select(3)) decoder_3 (
    .out0(decoder_3_out0), .out1(decoder_3_out1), .out2(decoder_3_out2), .out3(decoder_3_out3),
    .out4(decoder_3_out4), .out5(decoder_3_out5), .out6(decoder_3_out6), .out7(decoder_3_out7),
    .sel({or_8_out[2], register_4_q[1:0]}), .en(decoder_1_out3));
  or or_8 (or_8_out[2], register_4_q[2], and_10_out);
  or or_9 (or_9_out[2], rom_1_data[8], register_3_q[2]);
  and and_17 (and_17_out, c, and_14_out);
  and and_18 (and_18_out, z, and_15_out);
  and and_19 (and_19_out, n, and_16_out);
  not not_14 (not_14_out, counter_1_q[0]);
  Priority_Encoder #(.select(2)) priority_encoder_1 (
    .in0(register_4_q[4]), .in1(register_4_q[5]), .in2(register_4_q[6]), .in3(register_4_q[7]),
    .out(priority_encoder_1_out));  // open: gs, en_out, en_in
  Decoder #(.select(2)) decoder_4 (
    .out0(decoder_4_out0), .out1(decoder_4_out1), .out2(decoder_4_out2), .out3(decoder_4_out3),
    .sel(priority_encoder_1_out), .en(and_20_out));
  and and_20 (and_20_out, inp, rd);
  Decoder #(.select(3)) decoder_5 (
    .out0(decoder_5_out0), .out1(decoder_5_out1), .out2(decoder_5_out2), .out3(decoder_5_out3),
    .out4(decoder_5_out4), .out5(decoder_5_out5), .out6(decoder_5_out6), .out7(decoder_5_out7),
    .sel({or_9_out[2], register_3_q[1:0]}), .en(decoder_2_out2));
  or or_10 (or_10_out, rom_1_data[0], and_21_out);
  and and_21 (and_21_out, or_11_out, and_9_out, and_22_out);
  or or_11 (or_11_out, and_17_out, and_18_out, and_19_out);
  and and_22 (and_22_out, not_14_out, counter_1_q[1], counter_1_q[2]);
  assign oPORT_d = decoder_4_out0 ? iPORT_0 : 8'bz;  // Controlled_Buffer controlled_buffer_2
  assign oPORT_d = decoder_3_out5 ? register_5_q : 8'bz;  // Controlled_Buffer controlled_buffer_3
  Register register_5 (.D(oPORT_d), .en(decoder_5_out5), .clk(and_1_out), .Q(register_5_q), .clr(rst));
  or or_12 (we, rom_1_data[6], decoder_5_out0);
  Multiplexer #(.width(16)) multiplexer_2 (
    .in0(register_10_q), .in1(register_11_q), .out(multiplexer_2_out), .sel(rom_1_data[3]));
  assign bit_extender_5_out = {{15{1'b0}}, 1'b1};  // Bit_Extender bit_extender_5
  assign bit_extender_6_out = {{15{1'b1}}, 1'b1};  // Bit_Extender bit_extender_6
  assign oPORT_d = decoder_4_out1 ? iPORT_1 : 8'bz;  // Controlled_Buffer controlled_buffer_4
  assign oPORT_d = decoder_3_out1 ? register_6_q : 8'bz;  // Controlled_Buffer controlled_buffer_5
  Register register_6 (.D(oPORT_d), .en(decoder_5_out1), .clk(and_1_out), .Q(register_6_q), .clr(rst));
  Adder #(.width(16)) adder_2 (.a(multiplexer_2_out), .b(multiplexer_3_out), .out(adder_2_out));  // open: cin, cout
  Multiplexer #(.width(16)) multiplexer_3 (
    .in0(bit_extender_5_out), .in1(bit_extender_6_out), .out(multiplexer_3_out), .sel(rom_1_data[2]));
  assign oPORT_d = decoder_4_out2 ? iPORT_2 : 8'bz;  // Controlled_Buffer controlled_buffer_6
  assign oPORT_d = decoder_4_out3 ? iPORT_3 : 8'bz;  // Controlled_Buffer controlled_buffer_7
  Register register_7 (.D(oPORT_d), .en(decoder_5_out6), .clk(and_1_out), .Q(register_7_q), .clr(rst));
  not not_15 (not_15_out, rom_1_data[1]);
  assign controlled_buffer_8_out = not_15_out ? adder_2_out : 16'bz;  // Controlled_Buffer controlled_buffer_8
  assign controlled_buffer_8_out = rom_1_data[1] ? wz : 16'bz;  // Controlled_Buffer controlled_buffer_9
  assign oPORT_d = decoder_3_out6 ? register_7_q : 8'bz;  // Controlled_Buffer controlled_buffer_10
  Register register_8 (.D(oPORT_d), .en(decoder_5_out2), .clk(and_1_out), .Q(register_8_q), .clr(rst));
  Decoder decoder_6 (.out0(decoder_6_out0), .out1(decoder_6_out1), .sel(rom_1_data[3]), .en(or_10_out));
  assign oPORT_d = decoder_3_out2 ? register_8_q : 8'bz;  // Controlled_Buffer controlled_buffer_11
  Register register_9 (.D(oPORT_d), .en(decoder_5_out7), .clk(and_1_out), .Q(register_9_q), .clr(rst));
  Register #(.width(16)) register_10 (
    .D(controlled_buffer_8_out), .en(decoder_6_out0), .clk(and_1_out), .Q(register_10_q), .clr(rst));
  Register #(.width(16)) register_11 (
    .D(controlled_buffer_8_out), .en(decoder_6_out1), .clk(and_1_out), .Q(register_11_q), .clr(rst));
  and and_23 (wr_0, rom_1_data[9], register_4_q[4]);
  and and_24 (wr_1, rom_1_data[9], register_4_q[5]);
  and and_25 (wr_2, rom_1_data[9], register_4_q[6]);
  and and_26 (wr_3, rom_1_data[9], register_4_q[7]);
  assign oPORT_d = decoder_3_out7 ? register_9_q : 8'bz;  // Controlled_Buffer controlled_buffer_12
  Register register_12 (.D(oPORT_d), .en(decoder_5_out3), .clk(and_1_out), .Q(register_12_q), .clr(rst));
  assign oPORT_d = decoder_3_out3 ? register_12_q : 8'bz;  // Controlled_Buffer controlled_buffer_13
  Multiplexer #(.select(2), .width(16)) multiplexer_4 (
    .in0({register_9_q, register_12_q}), .in1(register_10_q), .in2(register_11_q), .in3(wz),
    .out(multiplexer_4_out), .sel(rom_1_data_2));
  Multiplexer #(.width(8)) multiplexer_5 (
    .in0(register_10_q[7:0]), .in1(register_10_q[15:8]), .out(multiplexer_5_out), .sel(rom_1_data[8]));
  assign oPORT_d = decoder_3_out4 ? register_13_q : 8'bz;  // Controlled_Buffer controlled_buffer_14
  Register register_13 (.D(oPORT_d), .en(decoder_5_out4), .clk(and_1_out), .Q(register_13_q), .clr(rst));
  Multiplexer #(.width(8)) multiplexer_6 (.in0(oPORT_d), .in1(multiplexer_5_out), .out(DATA_o), .sel(rom_1_data[7]));
  Register register_14 (.D(oPORT_d), .en(rom_1_data[5]), .clk(and_1_out), .Q(register_14_q), .clr(rst));
  assign bit_extender_7_out = {{5{1'b0}}, 1'b0};  // Bit_Extender bit_extender_7
  and and_27 (and_27_out, multiplexer_4_out[15], multiplexer_4_out[14]);
  or or_13 (or_13_out, decoder_1_out0, decoder_3_out0);
  Multiplexer #(.width(22)) multiplexer_7 (
    .in0({bit_extender_7_out, multiplexer_4_out}), .in1({register_14_q, multiplexer_4_out[13:0]}),
    .out(addr), .sel(and_27_out));
  assign oPORT_d = or_13_out ? DATA_i : 8'bz;  // Controlled_Buffer controlled_buffer_15

  // Notes on the sheet:
  //   ALU
  //   contents of rom_1 (hex, n*v repeats v):
  //   31*400 0 31*3011 0 5*400 8*d500 d100 d100 d500 d100 d500 d500 400 d 800 400 800 7*400 0 11 2001 2101
  //   1101 1101 11 11 1001 1001 11 11 1001 1001 3a6000 186000 11 306000 11 11 1101 c840 2000 1101 1109
  //   1101 1101 1101 11 11 21 1101 0 e000 0 400 400 400 d000 d000 6000 16000 d000 d000 226000 236000 0 0
  //   d000 0 d000 d000 400 0 9 40d 800 400 400 400 a000 c200 0 400 0 0 0 2001 1001 1001 6000 16000 0 0
  //   226000 236000 4*0 224000 0 46000 2e6000 1001 0 0 1001 1009 1001 1001 1001 0 0 0 1001 4*0 c00 cc40
  //   14*0 3 0 0 8cd 3 2 2 2 0 0 0 b 4*0 2000 18*0 9c3
  //   B
  //   C
  //   PC/StackPointer
  //   D
  //   Memory Array
  //   E
  //   H
  //   L
  //   A
  //   address
endmodule

module test (
  input  [2:0] in_1,
  input  in_2
);

  wire clock_1_out, cpu_1_p1, cpu_1_p3, cpu_1_p6, cpu_1_p7, cpu_1_p10;
  wire [4:0] bit_extender_1_out;
  wire [5:0] bit_extender_2_out;
  wire [7:0] cpu_1_p4, cpu_1_p8, cpu_1_p11, register_1_q;
  wire [21:0] cpu_1_p9;

  Bit_Extender #(.out_width(5)) bit_extender_1 (.in(cpu_1_p4), .out(bit_extender_1_out));
  Clock clock_1 (.out(clock_1_out));
  Register register_1 (.D(cpu_1_p4), .en(cpu_1_p1), .clk(cpu_1_p6), .Q(register_1_q), .clr(in_2));
  Bit_Extender #(.out_width(6)) bit_extender_2 (.in(register_1_q), .out(bit_extender_2_out));
  // CPU cpu_1: pin names not known; wires that end beside it: cpu_1_p1, in_2, cpu_1_p3, cpu_1_p4, clock_1_out, cpu_1_p6, cpu_1_p7, cpu_1_p8, cpu_1_p9, cpu_1_p10, cpu_1_p11
  // RGB_Video #(.cursor("No Cursor"), .height(32), .scale(8), .width(64)) rgb_video_1: pin names not known; wires that end beside it: cpu_1_p7, cpu_1_p6, cpu_1_p3, bit_extender_2_out, bit_extender_1_out, in_1
  RAM #(.addrWidth(22)) ram_1 (
    .addr(cpu_1_p9), .we(cpu_1_p10), .oe(1'b1), .clk(cpu_1_p6), .din(cpu_1_p11), .dout(cpu_1_p8));
endmodule
